# Fritzing sketch FRITZINK (saved by Fritzing 0.9.3b)

parts:
  DC1 = DC_DC_XL4016 [package=board_screw]
  J1 = XL4015 DC-DC CC CV module (blue)
  J2 = Power Jack [package=power_jack_slot]
  J3 = Piezo Speaker
  J4 = Basic Servo
  A1 = nozzle-bolt style thermocouple [package=THT]
  U1 = MAX6675 [package=so08]
  A2 = DM860A Stepper Motor Driver
  M1 = Stepper Motor - Unipolar
  U2 = ESP32-38PinWide [part_number=ESP32-38PinWide]
  Q3 = NPN-Transistor [package="TO92 [THT]"]
  R3 = Resistor [tolerance=±5% resistance=220 package="0402 [SMD]"]
  A3 = DM860A Stepper Motor Driver
  M2 = Stepper Motor - Unipolar
  JL012-13-5_1 = JL012-13-5.2 Lever (Limit) Switch SPDT + NO + NC [part_number=JL012-13-5.2]
  JL012-13-5_2 = JL012-13-5.2 Lever (Limit) Switch SPDT + NO + NC [part_number=JL012-13-5.2]
  JL012-13-5_3 = JL012-13-5.2 Lever (Limit) Switch SPDT + NO + NC [part_number=JL012-13-5.2]
  JL012-13-5_4 = JL012-13-5.2 Lever (Limit) Switch SPDT + NO + NC [part_number=JL012-13-5.2]
  R4 = Resistor [tolerance=±5% resistance=220 package="0402 [SMD]"]
  Q4 = NPN-Transistor [package="TO92 [THT]"]
  R5 = Resistor [tolerance=±5% resistance=220 package="0402 [SMD]"]
  Q5 = NPN-Transistor [package="TO92 [THT]"]
  R6 = Resistor [tolerance=±5% resistance=220 package="0402 [SMD]"]
  R7 = Resistor [tolerance=±5% resistance=220 package="0402 [SMD]"]
  R8 = Resistor [tolerance=±5% resistance=220 package="0402 [SMD]"]
  Q6 = NPN-Transistor [package="TO92 [THT]"]
  Q7 = NPN-Transistor [package="TO92 [THT]"]
  Q8 = NPN-Transistor [package="TO92 [THT]"]
  R9 = Resistor [tolerance=±5% resistance=220 package="0402 [SMD]"]
  R10 = Resistor [tolerance=±5% resistance=220 package="0402 [SMD]"]
  R11 = Resistor [tolerance=±5% resistance=220 package="0402 [SMD]"]
  R12 = Resistor [tolerance=±5% resistance=220 package="0402 [SMD]"]
  D1 = Zener Diode [part_number=1N4732A breakdown_voltage=3.6V package="300 mil [THT]"]
  R13 = Resistor [tolerance=±5% resistance=220 package="0402 [SMD]"]
  Q9 = NPN-Transistor [package="TO92 [THT]"]

nets:
  N1: DC1.IN+, J1.pin_1, J2.GNDBREAK, A2.VDC, A3.VDC
  GND: DC1.IN-, J1.pin_2, J2.GND, A2.GND, A3.GND
  VCC: DC1.OUT+, J3.pin2, J4.vcc, U1.VDD, A2.ENBL+(+5V), A2.DIR+(+5V), A2.PUL+(+5V), A3.ENBL+(+5V), A3.DIR+(+5V), A3.PUL+(+5V), D1.cathode
  GND_2: DC1.OUT-, J4.gnd, U1.VSS, Q3.E, JL012-13-5_1.NC, JL012-13-5_2.NC, JL012-13-5_3.NC, JL012-13-5_4.NC, Q4.E, Q5.E, Q6.E, Q7.E, Q8.E, Q9.E
  N2: J1.pin_3, U2.VIN
  N3: J1.pin_4, U2.GPIO11
  N4: J3.pin1, D1.anode, Q9.C
  N5: J4.pulse, U2.GPIO13
  N6: A1.pin1, U1.T-
  N7: A1.pin2, U1.T+
  N8: U1.SCK, U2.GPIO18
  N9: U1.CS, U2.GPIO5
  N10: U1.MISO, U2.GPIO19
  N11: A2.B-, M1.D
  N12: A2.B+, M1.B
  N13: A2.A-, M1.C
  N14: A2.A+, M1.A
  N15: A2.ENBL-(ENB), Q3.C
  N16: A2.DIR-(DIR), Q4.C
  N17: A2.PUL-(PUL), Q5.C
  N18: U2.3.3, R9.Pin_1, R10.Pin_1, R11.Pin_1, R12.Pin_1
  N19: U2.GPIO39, JL012-13-5_3.NO, R12.Pin_0
  N20: U2.GPIO34, JL012-13-5_1.NO, R10.Pin_0
  N21: U2.GPIO35, JL012-13-5_2.NO, R11.Pin_0
  N22: U2.GPIO32, R5.Pin_1
  N23: U2.GPIO33, R4.Pin_1
  N24: U2.GPIO25, R3.Pin_1
  N25: U2.GPIO26, R7.Pin_1
  N26: U2.GPIO27, R8.Pin_1
  N27: U2.GPIO14, R6.Pin_1
  N28: U2.GPIO17, JL012-13-5_4.NO, R9.Pin_0
  N29: Q3.B, R3.Pin_0
  N30: A3.B-, M2.COMMON_2, M2.D
  N31: A3.B+, M2.B
  N32: A3.A-, M2.COMMON_1, M2.C
  N33: A3.A+, M2.A
  N34: A3.ENBL-(ENB), Q6.C
  N35: A3.DIR-(DIR), Q8.C
  N36: A3.PUL-(PUL), Q7.C
  N37: R4.Pin_0, Q4.B
  N38: R5.Pin_0, Q5.B
  N39: R6.Pin_0, Q6.B
  N40: R7.Pin_0, Q7.B
  N41: R8.Pin_0, Q8.B
  N42: R13.Pin_0, Q9.B

custom parts:
  DC_DC_XL4016: DC-DC Converter step down voltage regulator XL4016 custom sketch.
  XL4015 DC-DC CC CV module (blue): XL4015 DC-DC CC/CV module blue
  nozzle-bolt style thermocouple: Generic nozzle-bolt style thermocouple.
  DM860A Stepper Motor Driver: DM860A is a type of two-phase hybrid stepping motor driver, The drive voltage of which is from 24VDC to 80VDC. It is designed for use with 2-phase hybrid stepper motor of all kinds with 57mm to 110mm outside diameter and less than 8.0A phase current. Mar 2023: Correct pcb layerId as the part won't save correctly in a .fzz file as is.
  ESP32-38PinWide: Generic 38-Pin ESP32 with wide format (only access to one side of pins on a breadboard) based on Stephen Lilley's HiLetgo ESP-WROOM-32 ESP32 ESP-32S Development Board.
  JL012-13-5.2 Lever (Limit) Switch SPDT + NO + NC: Micro Switch; Model No.: JL012-13.5-2; Actuator Action: Momentary; Actuator Type: Hinge Lever; Contact Configuration: 1NO, 1NC (SPDT) Temperature -25~65℃；Relative humidity: below 85%; Rate Voltage: 125V AC; Rated Current: 1A.
